# Fritzing sketch pinLayout (saved by Fritzing 1.0.0rc)
breadboards: 1

parts:
  Raspberry_Pi_1 = Raspberry Pi 3 [part_number=RPI-3-V1.2]
  onoffshim1 = Pimoroni OnOffShim
  Grove1 = Grove OLED 128x96
  SP1 = SPEAKER [package=pcb_mount_speaker]
  SP2 = SPEAKER [package=pcb_mount_speaker]

nets:
  3V3: Raspberry_Pi_1.3v3, Raspberry_Pi_1.3V3, onoffshim1.pin_1
  N1: Raspberry_Pi_1.GPIO2, Grove1.SDA
  N2: Raspberry_Pi_1.GPIO3, Grove1.SCL
  N3: Raspberry_Pi_1.GPIO4, onoffshim1.pin_7
  GND: Raspberry_Pi_1.GND, onoffshim1.pin_6, Grove1.GND
  N4: Raspberry_Pi_1.GPIO17, onoffshim1.pin_11
  N5: Raspberry_Pi_1.GPIO19, SP2.-
  N6: Raspberry_Pi_1.GPIO21, SP1.-
  N7: Raspberry_Pi_1.GPIO20, SP2.+
  N8: Raspberry_Pi_1.GPIO18, SP1.+
  5V: Raspberry_Pi_1.5V, onoffshim1.pin_2, onoffshim1.pin_4, Grove1.VCC

notes:
  Pins 3V, 5V, GND
  GPIO 18
  GPIO 19
  GPIO 20
  GPIO 21
  LED-Pins
  prev=5 (Weiß) -> grün
  play=6 (Rot)
  next=22 (Lila)
  volup=24 (Grün) -> blau
  voldown=23 (Blau) -> Weiß
  Button Pins
  volU = Button(16,pull_up=True,hold_time=0.3,hold_repeat=True)
  volD = Button(13,pull_up=True,hold_time=0.3,hold_repeat=True)
  next = Button(26,pull_up=True,hold_time=2.0,hold_repeat=False)
  prev = Button(27,pull_up=True,hold_time=2.0,hold_repeat=False)
  halt = Button(12,pull_up=True)
  power = Button(17,pull_up=True,hold_time=0,hold_repeat=False)
